# Fritzing sketch l298n (saved by Fritzing 0.9.5d)
breadboards: 1

parts:
  Part1 = Arduino Uno (Rev3)
  S1 = H-Bridge with L298N
  R1 = Rotary Potentiometer (Small) [maximum_resistance=100kΩ package=THT]
  M1 = DC Motor
  BAT1 = BC9VPC [package=bc9vpc]
  S2 = Pushbutton [package="[THT]"]

nets:
  N1: Part1.A0, R1.wiper
  GND: Part1.GND, S1.GND, R1.leg2, BAT1.V-, S2.Pin_1, S2.Pin_2
  N2: Part1.D2, S2.Pin_3, S2.Pin_4
  N3: Part1.D3_PWM, S1.ENA
  N4: Part1.D6_PWM, S1.IN1
  N5: Part1.D7, S1.IN2
  N6: Part1.5V, R1.leg1
  N7: S1.12V, BAT1.V+
  N8: S1.M1-01, M1.pin_2
  N9: S1.M1-02, M1.pin_1

custom parts:
  H-Bridge with L298N: h-bridge
